# Fritzing sketch L02_01 helloLED (saved by Fritzing 1.0.4)
breadboards: 1

parts:
  A1 = Particle - Photon2
  R3 = Resistor [tolerance=±5% resistance=220 package="0805 [SMD]"]
  LED1 = LED - 5mm [color="Red (633nm)" current=0.030A package="5 mm [THT]"]

nets:
  N1: A1.Pin_4, R3.Pin_1
  N2: A1.Pin_18, LED1.anode
  N3: R3.Pin_0, LED1.cathode

custom parts:
  Particle - Photon2: The Photon 2 is a microcontroller and Wi-Fi networking developed by particle. Features: 802.11a/b/g/n Wi-Fi, 2.4 GHz and 5 GHz Integrated PCB antenna Integrated U.FL connector for external antenna Integrated RF switch BLE 5 using same antenna as Wi-Fi Realtek RTL8721DM MCU ARM Cortex M33 CPU, 200 MHz 2048 KB (2 MB) user application maximum size 3072 KB (3 MB) of RAM available to user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
